# Fritzing sketch template_fritzing(1) (saved by Fritzing 0.9.3b)
breadboards: 3

parts:
  JP1 = Header 12 [package=1x12_machine-pin-header_lock.004]
  JP2 = Header 12 [package=1x12_machine-pin-header_lock.004]
  J1 = Dagu DGServo 9g header connector (female) [package=THT]  # not connected
  C1 = Capacitor Polarized [package=cpol-radial-10uf-25v]
  C2 = Capacitor Polarized [package=cpol-radial-10uf-25v]
  J2 = Dagu DGServo 9g header connector (female) [package=THT]  # not connected
  J3 = Dagu DGServo 9g header connector (female) [package=THT]  # not connected
  C3 = Ceramic Capacitor [capacitance=100nF package="100 mil [THT, multilayer]"]
  C4 = Ceramic Capacitor [capacitance=100nF package="100 mil [THT, multilayer]"]
  U1 = OP27 - Low Noise, Precision Op Amp [part_number=OP27]
  U2 = OP27 - Low Noise, Precision Op Amp [part_number=OP27]  # not connected
  U3 = OP27 - Low Noise, Precision Op Amp [part_number=OP27]  # not connected
  U4 = OP27 - Low Noise, Precision Op Amp [part_number=OP27]  # not connected
  U5 = OP27 - Low Noise, Precision Op Amp [part_number=OP27]  # not connected
  U6 = OP27 - Low Noise, Precision Op Amp [part_number=OP27]  # not connected
  U7 = OP27 - Low Noise, Precision Op Amp [part_number=OP27]  # not connected
  U8 = OP27 - Low Noise, Precision Op Amp [part_number=OP27]  # not connected
  U9 = OP27 - Low Noise, Precision Op Amp [part_number=OP27]  # not connected
  U10 = OP27 - Low Noise, Precision Op Amp [part_number=OP27]  # not connected
  U11 = OP27 - Low Noise, Precision Op Amp [part_number=OP27]  # not connected
  U12 = OP27 - Low Noise, Precision Op Amp [part_number=OP27]  # not connected
  U13 = OP27 - Low Noise, Precision Op Amp [part_number=OP27]  # not connected

nets:
  N1: JP1.1, JP2.1, C1.-
  N2: JP1.2, JP2.2, C1.+, C2.+
  N3: JP1.3, JP2.3, C2.-
  N4: JP1.4, JP2.4
  N5: JP1.5, JP2.5
  N6: JP1.6, JP2.6
  N7: JP1.7, JP2.7
  N8: JP1.8, JP2.8
  N9: JP1.9, JP2.9
  N10: JP1.10, JP2.10
  N11: JP1.11, JP2.11
  N12: JP1.12, JP2.12
  N13: C3.0, C4.1
  N14: C3.1, U1.V+
  N15: C4.0, U1.-V

notes:
  Fargekoding:
  Rød: V+
  Blå: V-
  Sort: GND
  Mal for Analog motorlab
  Kretsen kan også tegnes på papir eller ved bruk av andre programmer. Det som er viktig er at dere har en plan for hvordan dere skal koble kretsen når dere kommer på lab.
  TTK4101 Instrumentering og måleteknikk
  2018 Eivind H. Jølsgard
